# Fritzing sketch SelfBalance (saved by Fritzing 0.9.3b)

parts:
  M2 = Stepper Motor - Bipolar
  M3 = Stepper Motor - Bipolar
  U1 = ESP32S-HiLetgo [part_number=ESP32S-HiLetgo]
  Part1 = InvenSense MPU6050
  DRV_1 = DRV 8825 Stepper Motor Carrier, High Current [part_number="DRV 8825"]
  DRV_2 = DRV 8825 Stepper Motor Carrier, High Current [part_number="DRV 8825"]

nets:
  N1: M2.A, DRV_1.OUT_2B
  N2: M2.C, DRV_1.OUT_2A
  N3: M2.B, DRV_1.OUT_1A
  N4: M2.D, DRV_1.OUT_1B
  N5: M3.A, DRV_2.OUT_2B
  N6: M3.C, DRV_2.OUT_2A
  N7: M3.B, DRV_2.OUT_1A
  N8: M3.D, DRV_2.OUT_1B
  N9: U1.3.3, Part1.VCC, DRV_1.MS3, DRV_2.MS3
  N10: U1.GPIO25, DRV_1.DIRECTION
  N11: U1.GPIO26, DRV_1.STEP
  N12: U1.GPIO27, DRV_2.DIRECTION
  N13: U1.GPIO14, DRV_2.STEP
  N14: U1.GPIO12, DRV_1.ENABLE, DRV_2.ENABLE
  GND: U1.GND, Part1.GND, DRV_1.MS1, DRV_1.GROUND_LOG, DRV_2.MS1, DRV_2.GROUND_LOG
  N15: U1.GPIO21, Part1.SDA
  N16: U1.GPIO22, Part1.SCL
  N17: DRV_1.MS2, DRV_2.MS2
  N18: DRV_1.RESET, DRV_2.RESET
  N19: DRV_1.SLEEP, DRV_2.SLEEP

custom parts:
  ESP32S-HiLetgo: HiLetgo ESP-WROOM-32 ESP32 ESP-32S Development Board 2.4GHz Dual-Mode WiFi + Bluetooth Dual Cores Microcontroller The ESP32 integrated with Antenna switches, RF Balun, power amplifiers, low-noise amplifiers, filters, and management modules, and the entire solution occupies the least area of PCB. 2.4 GHz Wi-Fi plus Bluetooth dual-mode chip, with TSMC Ultra-low power consumption 40nm technology,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
