# Fritzing sketch self_balance_correct (saved by Fritzing 0.9.3b)
breadboards: 1

parts:
  U1 = NodeMCU V1.0
  Part1 = InvenSense MPU6050
  Pololu_A1 = Pololu A4988 [package=SO16]
  Pololu_A2 = Pololu A4988 [package=SO16]
  M1 = Stepper Motor - Bipolar
  M2 = Stepper Motor - Bipolar
  U2 = LIPO-2000mAh [package=lipo-2000]

nets:
  N1: U1.D1, Part1.SCL
  N2: U1.D2, Part1.SDA
  N3: U1.D3, Pololu_A1.STEP
  N4: U1.D4, Pololu_A1.DIR
  VDD: U1.3V3, Part1.VCC, Pololu_A1.VDD, Pololu_A2.VDD
  GND: U1.GND, Part1.GND, Pololu_A1.GND, Pololu_A2.GND, U2.-
  N5: U1.D6, Pololu_A2.STEP
  N6: U1.D7, Pololu_A2.DIR
  N7: U1.Vin, Pololu_A1.VMOT, Pololu_A2.VMOT, U2.+
  N8: Pololu_A1.RESET, Pololu_A1.SLEEP
  N9: Pololu_A1.1B, M2.D
  N10: Pololu_A1.1A, M2.B
  N11: Pololu_A1.2A, M2.A
  N12: Pololu_A1.2B, M2.C
  N13: Pololu_A2.RESET, Pololu_A2.SLEEP
  N14: Pololu_A2.1B, M1.C
  N15: Pololu_A2.1A, M1.A
  N16: Pololu_A2.2A, M1.B
  N17: Pololu_A2.2B, M1.D

custom parts:
  NodeMCU V1.0: ESP8266 based NodeMCU
